// Logisim project relogio-digital.circ as structural Verilog: 3 circuits, main circuit main
module main (
  input  Led
);

  wire and_1_out, and_2_out, and_3_out, and_4_out, and_5_out, and_6_out, and_7_out, and_8_out, and_9_out,
       contador_2_a, contador_2_b, contador_2_c, contador_2_d, contador_3_a, contador_3_b, contador_3_c,
       contador_3_d, contador_4_a, contador_4_b, contador_4_c, contador_4_d, contador_5_a, contador_5_b,
       contador_5_c, contador_5_d, contador_6_a, contador_6_b, contador_6_c, contador_6_d, contador_7_a,
       contador_7_b, contador_7_c, contador_7_d, Contador_out, decodificador_1_a, decodificador_1_b,
       decodificador_1_c, decodificador_1_d, decodificador_1_e, decodificador_1_f, decodificador_1_g,
       decodificador_2_a, decodificador_2_b, decodificador_2_c, decodificador_2_d, decodificador_2_e,
       decodificador_2_f, decodificador_2_g, decodificador_3_a, decodificador_3_b, decodificador_3_c,
       decodificador_3_d, decodificador_3_e, decodificador_3_f, decodificador_3_g, decodificador_4_a,
       decodificador_4_b, decodificador_4_c, decodificador_4_d, decodificador_4_e, decodificador_4_f,
       decodificador_4_g, decodificador_5_a, decodificador_5_b, decodificador_5_c, decodificador_5_d,
       decodificador_5_e, decodificador_5_f, decodificador_5_g, decodificador_6_a, decodificador_6_b,
       decodificador_6_c, decodificador_6_d, decodificador_6_e, decodificador_6_f, decodificador_6_g,
       or_1_out, or_2_out, or_3_out, or_4_out, or_5_out, or_6_out, or_7_out, Resetar_out;

  Clock Contador (.out(Contador_out));
  Button Resetar (.out(Resetar_out));
  and and_1 (and_1_out, contador_2_a, contador_2_b, ~contador_2_d, ~contador_2_d);  // AND_Gate
  or or_1 (or_1_out, Resetar_out, and_1_out);
  and and_2 (and_2_out, ~contador_2_a, contador_2_b, ~contador_2_c, ~contador_2_d);  // AND_Gate
  Contador contador_2 (
    .Entrada(or_2_out), .Reset(and_1_out), .a(contador_2_a), .b(contador_2_b), .c(contador_2_c),
    .d(contador_2_d));
  Decodificador decodificador_1 (
    .A1(contador_2_d), .A2(contador_2_c), .A3(contador_2_b), .A4(contador_2_a), .a(decodificador_1_a),
    .b(decodificador_1_b), .c(decodificador_1_c), .d(decodificador_1_d), .e(decodificador_1_e),
    .f(decodificador_1_f), .g(decodificador_1_g));
  _7_Segment_Display u_7_segment_display_1 (
    .g(decodificador_1_g), .f(decodificador_1_f), .a(decodificador_1_a), .b(decodificador_1_b),
    .e(decodificador_1_e), .d(decodificador_1_d), .c(decodificador_1_c));  // open: dp
  or or_2 (or_2_out, and_3_out, and_5_out);
  and and_3 (and_3_out, and_2_out, and_4_out);
  and and_4 (and_4_out, ~contador_3_a, ~contador_3_b, contador_3_c, ~contador_3_d);  // AND_Gate
  Contador contador_3 (
    .Entrada(and_6_out), .Reset(or_3_out), .a(contador_3_a), .b(contador_3_b), .c(contador_3_c),
    .d(contador_3_d));
  _7_Segment_Display u_7_segment_display_2 (
    .g(decodificador_2_g), .f(decodificador_2_f), .a(decodificador_2_a), .b(decodificador_2_b),
    .e(decodificador_2_e), .d(decodificador_2_d), .c(decodificador_2_c));  // open: dp
  or or_3 (or_3_out, or_1_out, or_2_out);
  and and_5 (and_5_out, ~contador_3_a, contador_3_b, ~contador_3_c, contador_3_d);  // AND_Gate
  Decodificador decodificador_2 (
    .A1(contador_3_d), .A2(contador_3_c), .A3(contador_3_b), .A4(contador_3_a), .a(decodificador_2_a),
    .b(decodificador_2_b), .c(decodificador_2_c), .d(decodificador_2_d), .e(decodificador_2_e),
    .f(decodificador_2_f), .g(decodificador_2_g));
  LED led_1 (.in(Led));
  LED led_2 (.in(Led));
  and and_6 (and_6_out, ~contador_4_a, contador_4_b, contador_4_c, ~contador_4_d);  // AND_Gate
  Contador contador_4 (
    .Entrada(and_7_out), .Reset(or_4_out), .a(contador_4_a), .b(contador_4_b), .c(contador_4_c),
    .d(contador_4_d));
  _7_Segment_Display u_7_segment_display_3 (
    .g(decodificador_3_g), .f(decodificador_3_f), .a(decodificador_3_a), .b(decodificador_3_b),
    .e(decodificador_3_e), .d(decodificador_3_d), .c(decodificador_3_c));  // open: dp
  or or_4 (or_4_out, or_1_out, and_6_out);
  Contador contador_5 (
    .Entrada(and_8_out), .Reset(or_5_out), .a(contador_5_a), .b(contador_5_b), .c(contador_5_c),
    .d(contador_5_d));
  Decodificador decodificador_3 (
    .A1(contador_4_d), .A2(contador_4_c), .A3(contador_4_b), .A4(contador_4_a), .a(decodificador_3_a),
    .b(decodificador_3_b), .c(decodificador_3_c), .d(decodificador_3_d), .e(decodificador_3_e),
    .f(decodificador_3_f), .g(decodificador_3_g));
  _7_Segment_Display u_7_segment_display_4 (
    .g(decodificador_4_g), .f(decodificador_4_f), .a(decodificador_4_a), .b(decodificador_4_b),
    .e(decodificador_4_e), .d(decodificador_4_d), .c(decodificador_4_c));  // open: dp
  or or_5 (or_5_out, or_1_out, and_7_out);
  and and_7 (and_7_out, ~contador_5_a, contador_5_b, ~contador_5_c, contador_5_d);  // AND_Gate
  Decodificador decodificador_4 (
    .A1(contador_5_d), .A2(contador_5_c), .A3(contador_5_b), .A4(contador_5_a), .a(decodificador_4_a),
    .b(decodificador_4_b), .c(decodificador_4_c), .d(decodificador_4_d), .e(decodificador_4_e),
    .f(decodificador_4_f), .g(decodificador_4_g));
  Contador contador_6 (
    .Entrada(and_9_out), .Reset(or_6_out), .a(contador_6_a), .b(contador_6_b), .c(contador_6_c),
    .d(contador_6_d));
  _7_Segment_Display u_7_segment_display_5 (
    .g(decodificador_5_g), .f(decodificador_5_f), .a(decodificador_5_a), .b(decodificador_5_b),
    .e(decodificador_5_e), .d(decodificador_5_d), .c(decodificador_5_c));  // open: dp
  LED led_3 (.in(Led));
  LED led_4 (.in(Led));
  or or_6 (or_6_out, or_1_out, and_8_out);
  and and_8 (and_8_out, ~contador_6_a, contador_6_b, contador_6_c, ~contador_6_d);  // AND_Gate
  Decodificador decodificador_5 (
    .A1(contador_6_d), .A2(contador_6_c), .A3(contador_6_b), .A4(contador_6_a), .a(decodificador_5_a),
    .b(decodificador_5_b), .c(decodificador_5_c), .d(decodificador_5_d), .e(decodificador_5_e),
    .f(decodificador_5_f), .g(decodificador_5_g));
  or or_7 (or_7_out, or_1_out, and_9_out);
  and and_9 (and_9_out, ~contador_7_a, contador_7_b, ~contador_7_c, contador_7_d);  // AND_Gate
  Contador contador_7 (
    .Entrada(Contador_out), .Reset(or_7_out), .a(contador_7_a), .b(contador_7_b), .c(contador_7_c),
    .d(contador_7_d));
  Decodificador decodificador_6 (
    .A1(contador_7_d), .A2(contador_7_c), .A3(contador_7_b), .A4(contador_7_a), .a(decodificador_6_a),
    .b(decodificador_6_b), .c(decodificador_6_c), .d(decodificador_6_d), .e(decodificador_6_e),
    .f(decodificador_6_f), .g(decodificador_6_g));
  _7_Segment_Display u_7_segment_display_6 (
    .g(decodificador_6_g), .f(decodificador_6_f), .a(decodificador_6_a), .b(decodificador_6_b),
    .e(decodificador_6_e), .d(decodificador_6_d), .c(decodificador_6_c));  // open: dp
endmodule

module Decodificador (
  input  A1,
  input  A2,
  input  A3,
  input  A4,
  output a,
  output b,
  output c,
  output d,
  output e,
  output f,
  output g
);

  wire and_1_out, and_2_out, and_3_out, and_4_out, and_5_out, and_6_out, and_7_out, and_8_out, and_9_out,
       and_10_out, and_11_out, and_12_out, and_13_out, and_14_out, and_15_out, and_16_out, and_17_out,
       and_18_out, and_19_out, and_20_out, and_21_out, and_22_out, and_23_out, and_24_out, and_25_out,
       and_26_out, not_1_out, not_2_out, not_3_out, not_4_out, not_5_out, not_6_out, not_7_out, not_8_out,
       not_9_out, not_10_out, not_11_out, not_12_out, not_13_out, not_14_out, not_15_out, not_16_out,
       not_17_out, not_18_out, not_19_out, not_20_out, not_21_out, not_22_out, not_23_out, not_24_out,
       not_25_out, not_26_out, not_27_out, not_28_out, not_29_out, not_30_out, not_31_out, not_32_out,
       not_33_out, not_34_out, not_35_out, not_36_out, not_37_out, not_38_out, not_39_out, not_40_out,
       not_41_out, not_42_out, not_43_out, not_44_out, not_45_out, not_46_out, not_47_out, not_48_out,
       not_49_out, not_50_out, not_51_out, not_52_out;

  not not_1 (not_1_out, A1);
  not not_2 (not_2_out, A2);
  and and_1 (and_1_out, not_1_out, not_2_out, not_3_out);
  not not_3 (not_3_out, A4);
  not not_4 (not_4_out, A1);
  and and_2 (and_2_out, not_4_out, A3);
  not not_5 (not_5_out, A1);
  and and_3 (and_3_out, not_5_out, A2, A4);
  and and_4 (and_4_out, A1, not_6_out, not_7_out);
  not not_6 (not_6_out, A2);
  not not_7 (not_7_out, A3);
  not not_8 (not_8_out, A1);
  and and_5 (and_5_out, not_8_out, not_9_out);
  not not_9 (not_9_out, A2);
  not not_10 (not_10_out, A1);
  and and_6 (and_6_out, not_10_out, not_11_out, not_12_out);
  not not_11 (not_11_out, A3);
  not not_12 (not_12_out, A4);
  not not_13 (not_13_out, A2);
  and and_7 (and_7_out, not_13_out, not_14_out);
  not not_14 (not_14_out, A3);
  not not_15 (not_15_out, A1);
  and and_8 (and_8_out, not_15_out, A3, A4);
  not not_16 (not_16_out, A2);
  and and_9 (and_9_out, not_16_out, not_17_out);
  not not_17 (not_17_out, A3);
  not not_18 (not_18_out, A1);
  and and_10 (and_10_out, not_18_out, A4);
  not not_19 (not_19_out, A1);
  and and_11 (and_11_out, not_19_out, A2);
  not not_20 (not_20_out, A1);
  not not_21 (not_21_out, A2);
  not not_22 (not_22_out, A4);
  not not_23 (not_23_out, A1);
  not not_24 (not_24_out, A2);
  not not_25 (not_25_out, A1);
  not not_26 (not_26_out, A4);
  not not_27 (not_27_out, A1);
  not not_28 (not_28_out, A3);
  not not_29 (not_29_out, A2);
  not not_30 (not_30_out, A3);
  not not_31 (not_31_out, A2);
  and and_12 (and_12_out, not_31_out, not_32_out, not_33_out);
  not not_32 (not_32_out, A3);
  not not_33 (not_33_out, A4);
  not not_34 (not_34_out, A1);
  and and_13 (and_13_out, not_34_out, A3, not_35_out);
  not not_35 (not_35_out, A4);
  not not_36 (not_36_out, A1);
  and and_14 (and_14_out, not_36_out, not_37_out, not_38_out);
  not not_37 (not_37_out, A3);
  not not_38 (not_38_out, A4);
  not not_39 (not_39_out, A1);
  and and_15 (and_15_out, not_39_out, A2, not_40_out);
  not not_40 (not_40_out, A3);
  not not_41 (not_41_out, A1);
  and and_16 (and_16_out, not_41_out, A2, not_42_out);
  not not_42 (not_42_out, A4);
  and and_17 (and_17_out, A1, not_43_out, not_44_out);
  not not_43 (not_43_out, A2);
  not not_44 (not_44_out, A3);
  not not_45 (not_45_out, A1);
  not not_46 (not_46_out, A2);
  and and_18 (and_18_out, not_45_out, not_46_out, A3);
  not not_47 (not_47_out, A1);
  and and_19 (and_19_out, not_47_out, A2, not_48_out);
  not not_48 (not_48_out, A3);
  not not_49 (not_49_out, A1);
  and and_20 (and_20_out, not_49_out, A2, not_50_out);
  not not_50 (not_50_out, A4);
  and and_21 (and_21_out, A1, not_51_out, not_52_out);
  not not_51 (not_51_out, A2);
  not not_52 (not_52_out, A3);
  or or_1 (a, and_1_out, and_2_out, and_3_out, and_4_out);
  or or_2 (b, and_5_out, and_6_out, and_7_out, and_8_out);
  or or_3 (c, and_9_out, and_10_out, and_11_out);
  and and_22 (and_22_out, not_20_out, not_21_out, not_22_out);
  and and_23 (and_23_out, not_23_out, not_24_out, A3);
  and and_24 (and_24_out, not_25_out, A3, not_26_out);
  and and_25 (and_25_out, not_27_out, A2, not_28_out, A4);
  and and_26 (and_26_out, A1, not_29_out, not_30_out);
  or or_4 (e, and_12_out, and_13_out);
  or or_5 (f, and_14_out, and_15_out, and_16_out, and_17_out);
  or or_6 (g, and_18_out, and_19_out, and_20_out, and_21_out);
  or or_7 (d, and_22_out, and_23_out, and_24_out, and_25_out, and_26_out);
endmodule

module Contador (
  input  Entrada,
  input  Reset,
  output a,
  output b,
  output c,
  output d
);

  Counter #(.width(4), .max('hf)) counter_1 (
    .Q({d, c, b, a}), .clk(Entrada), .clr(Reset));  // open: load, D, count, carry
endmodule
